# Fritzing sketch HC-05 to Motorshield (saved by Fritzing 0.9.3b)
breadboards: 1

parts:
  Part1 = Rotoshield - Motor driver shield for Arduino
  Part2 = Bluetooth HC-05 Macho
  R1 = Resistor [tolerance=±5% resistance=100 package=THT]
  R2 = Resistor [tolerance=±5% resistance=100 package=THT]
  R3 = Resistor [tolerance=±5% resistance=100 package=THT]

nets:
  N1: Part1.A_IN_0, R1.Pin_1
  N2: Part1.A_IN_1, Part2.TXD
  +5V: Part1.+5V, Part2.VCC
  GND: Part1.GND, Part2.GND, R3.Pin_0
  N3: Part2.RXD, R1.Pin_0, R2.Pin_1
  N4: R2.Pin_0, R3.Pin_1
